// Logisim project alu.circ as structural Verilog: 1 circuit, main circuit alu
module alu (
  input  [31:0] A,
  input  [31:0] B,
  input  [3:0] ALUSel,
  output [31:0] Result
);

  wire xor_3_out;
  wire [0:0] add7;
  wire [31:0] add0, add1, add2, add3, add4, add5, add6, add8, add9, add10, add11, add12, add14,
       multiplexer_1_out, multiplexer_2_out, multiplier_3_cout, not_1_out, not_2_out, not_3_out;

  Comparator #(.width(32)) comparator_1 (.a(A), .b(B), .lt(add7[0]));  // open: gt, eq
  Divider #(.width(32)) divider_1 (.a(A), .b(B), .out(add8));  // open: upper, rem
  Divider #(.width(32)) divider_2 (.a(A), .b(B), .rem(add9));  // open: out, upper
  Multiplier #(.width(32)) multiplier_1 (.a(A), .b(B), .cout(add11));  // open: out, cin
  Multiplier #(.width(31)) multiplier_2 (.a(A[30:0]), .b(B[30:0]), .out(add10[30:0]));  // open: cin, cout
  xor xor_1 (add10[31], A[31], B[31]);
  Adder #(.width(32)) adder_1 (.a(A), .b(B), .out(add0));  // open: cin, cout
  assign add1 = A & B;  // AND_Gate and_1, 32 bits wide
  assign add2 = A | B;  // OR_Gate or_1, 32 bits wide
  assign add3 = A ^ B;  // XOR_Gate xor_2, 32 bits wide
  Shifter #(.width(32), .shift("lr")) shifter_1 (.in(A), .\dist (B[4:0]), .out(add4));
  Shifter #(.width(32), .shift("ar")) shifter_2 (.in(A), .\dist (B[4:0]), .out(add5));
  Shifter #(.width(32)) shifter_3 (.in(A), .\dist (B[4:0]), .out(add6));
  assign not_1_out = ~A;  // NOT_Gate not_1, 32 bits wide
  assign not_2_out = ~B;  // NOT_Gate not_2, 32 bits wide
  Subtractor #(.width(32)) subtractor_1 (.a(A), .b(B), .out(add12));  // open: bin, bout
  Multiplexer #(.width(32), .enable("false")) multiplexer_1 (
    .in0(A), .in1(not_1_out), .out(multiplexer_1_out), .sel(A[31]));
  Multiplexer #(.width(32), .enable("false")) multiplexer_2 (
    .in0(B), .in1(not_2_out), .out(multiplexer_2_out), .sel(B[31]));
  Multiplier #(.width(32)) multiplier_3 (
    .a(multiplexer_1_out), .b(multiplexer_2_out), .cout(multiplier_3_cout));  // open: out, cin
  Multiplexer #(.select(4), .width(32), .enable("false")) multiplexer_3 (
    .in0(add0), .in1(add1), .in2(add2), .in3(add3), .in4(add4), .in5(add5), .in6(add6),
    .in7({{31{1'b0}}, add7[0]}), .in8(add8), .in9(add9), .in10(add10), .in11(add11), .in12(add12), .in13(B),
    .in14(add14), .out(Result), .sel(ALUSel));  // open: in15
  assign not_3_out = ~multiplier_3_cout;  // NOT_Gate not_3, 32 bits wide
  xor xor_3 (xor_3_out, A[31], B[31]);
  Multiplexer #(.width(32), .enable("false")) multiplexer_4 (
    .in0(multiplier_3_cout), .in1(not_3_out), .out(add14), .sel(xor_3_out));

  // Other names for the same wires on the sheet: add13[31:0] = B

  // Notes on the sheet:
  //   INPUTS to your circuit
  //   DON'T CHANGE THE LOCATIONS OF THE INPUTS AND OUTPUTS!
  //   OUTPUT from your circuit
endmodule
