// Logisim project cpu.circ as structural Verilog: 2 circuits, main circuit main
module main (
  input  [31:0] INSTRUCTION,
  input  CLOCK,
  output [31:0] PROGRAM_COUNTER,
  output [31:0] ra,
  output [31:0] sp,
  output [31:0] t0,
  output [31:0] t1,
  output [31:0] t2,
  output [31:0] s0,
  output [31:0] s1,
  output [31:0] a0
);

  wire comparator_1_eq;
  wire [4:0] rd_IF;
  wire [20:0] multiplexer_1_out;
  wire [31:0] adder_1_out, alu_result, multiplexer_2_out, multiplexer_3_out, Read_data, rs1_output, undriven,
       write_reg;

  imme imme_1 ();
  Adder #(.width(32)) adder_1 (.a(PROGRAM_COUNTER), .b(32'h4), .out(adder_1_out));  // open: cin, cout
  Register #(.width(32)) PC (.D(adder_1_out), .en(1'b1), .clk(CLOCK), .Q(PROGRAM_COUNTER));  // open: clr
  Multiplexer #(.width(21), .enable("false")) multiplexer_1 (
    .in0({21{1'b0}}), .in1({21{1'b1}}), .out(multiplexer_1_out), .sel(INSTRUCTION[31]));
  Register #(.width(5)) register_1 (.D(INSTRUCTION[11:7]), .en(1'b1), .clk(CLOCK), .Q(rd_IF));  // open: clr
  Multiplexer #(.width(32), .enable("false")) multiplexer_2 (
    .in0(Read_data), .in1(alu_result), .out(multiplexer_2_out), .sel(1'b1));
  Register #(.width(32)) register_2 (.D(multiplexer_2_out), .en(1'b1), .clk(CLOCK), .Q(write_reg));  // open: clr
  regfile_main RegFile (
    .rd(rd_IF), .Read_Data_1(rs1_output), .ra(ra), .sp(sp), .t0(t0), .t1(t1), .t2(t2), .s0(s0), .s1(s1),
    .a0(a0), .rs1(INSTRUCTION[19:15]), .Write_Data(write_reg), .RegWEn(1'b1), .clk(CLOCK));  // open: rs2, Read_Data_2
  Comparator #(.width(5)) comparator_1 (.a(INSTRUCTION[19:15]), .b(rd_IF), .eq(comparator_1_eq));  // open: gt, lt
  Multiplexer #(.width(32), .enable("false")) multiplexer_3 (
    .in0(rs1_output), .in1(write_reg), .out(multiplexer_3_out), .sel(comparator_1_eq));
  alu Arithmetic_Logic_Unit (.ALUSel(4'b0000), .B(undriven), .A(multiplexer_3_out), .Result(alu_result));
  // mem_main DMEM: pin names not known; wires that end beside it: CLOCK, Read_data

  // Other names for the same wires on the sheet: imm[11:0] = INSTRUCTION[31:20]; clk = CLOCK;
  //   opcode[6:0] = INSTRUCTION[6:0]; rd[4:0] = INSTRUCTION[11:7]; funct3[2:0] = INSTRUCTION[14:12];
  //   rs1[4:0] = INSTRUCTION[19:15]

  // Notes on the sheet:
  //   Output
  //   IMEM (do **NOT** move this)
  //   Inputs
  //   It is OK to move the PC, RegFile, ALU, and MEM to wherever is most convenient for you when constructing your CPU, and to delete this text
  //   Inputs/Outputs for testing. Do **NOT** move these.
endmodule

module imme (
);

  wire [31:11] I, S;
  wire [31:12] SB;
  wire [31:20] UJ;
  wire [31:31] INSTRUCTION;

  Multiplexer #(.width(21), .enable("false")) multiplexer_1 (
    .in0({21{1'b0}}), .in1({21{1'b1}}), .out(I), .sel(INSTRUCTION[31]));
  Multiplexer #(.width(21), .enable("false")) multiplexer_2 (
    .in0({21{1'b0}}), .in1({21{1'b1}}), .out(S), .sel(INSTRUCTION[31]));
  Multiplexer #(.width(20), .enable("false")) multiplexer_3 (
    .in0({20{1'b0}}), .in1({20{1'b1}}), .out(SB), .sel(INSTRUCTION[31]));
  Multiplexer #(.width(12), .enable("false")) multiplexer_4 (
    .in0({12{1'b0}}), .in1({12{1'b1}}), .out(UJ), .sel(INSTRUCTION[31]));

  // Other names for the same wires on the sheet: U[31] = INSTRUCTION[31]
endmodule
