// Logisim project alu.circ as structural Verilog: 1 circuit, main circuit alu
module alu (
  input  [31:0] A,
  input  [31:0] B,
  input  [3:0] ALUSel,
  output [31:0] Result
);

  wire [0:0] add7;
  wire [30:0] multiplier_3_out;
  wire [31:0] add0, add1, add2, add3, add4, add5, add6, add8, add9, add10, add11, add12, add14,
       multiplier_3_cout;

  Comparator #(.width(32)) comparator_1 (.a(A), .b(B), .lt(add7[0]));  // open: gt, eq
  Divider #(.width(32)) divider_1 (.a(A), .b(B), .out(add8));  // open: upper, rem
  Divider #(.width(32)) divider_2 (.a(A), .b(B), .rem(add9));  // open: out, upper
  Multiplier #(.width(32)) multiplier_1 (.a(A), .b(B), .cout(add11));  // open: out, cin
  Multiplier #(.width(31)) multiplier_2 (.a(A[30:0]), .b(B[30:0]), .out(add10[30:0]));  // open: cin, cout
  xor xor_1 (add10[31], A[31], B[31]);
  Adder #(.width(32)) adder_1 (.a(A), .b(B), .out(add0));  // open: cin, cout
  assign add1 = A & B;  // AND_Gate and_1, 32 bits wide
  assign add2 = A | B;  // OR_Gate or_1, 32 bits wide
  assign add3 = A ^ B;  // XOR_Gate xor_2, 32 bits wide
  Shifter #(.width(32), .shift("lr")) shifter_1 (.in(A), .\dist (B[4:0]), .out(add4));
  Shifter #(.width(32), .shift("ar")) shifter_2 (.in(A), .\dist (B[4:0]), .out(add5));
  Shifter #(.width(32)) shifter_3 (.in(A), .\dist (B[4:0]), .out(add6));
  Subtractor #(.width(32)) subtractor_1 (.a(A), .b(B), .out(add12));  // open: bin, bout
  Multiplier #(.width(32)) multiplier_3 (
    .a(A), .b(B), .out({add14[0], multiplier_3_out}),
    .cout({multiplier_3_cout[31], add14[30:1], multiplier_3_cout[0]}));  // open: cin
  xor xor_3 (add14[31], A[31], B[31]);
  Multiplexer #(.select(4), .width(32), .enable("false")) multiplexer_1 (
    .in0(add0), .in1(add1), .in2(add2), .in3(add3), .in4(add4), .in5(add5), .in6(add6),
    .in7({{31{1'b0}}, add7[0]}), .in8(add8), .in9(add9), .in10(add10), .in11(add11), .in12(add12), .in13(B),
    .in14(add14), .out(Result), .sel(ALUSel));  // open: in15

  // Other names for the same wires on the sheet: add13[31:0] = B

  // Notes on the sheet:
  //   INPUTS to your circuit
  //   DON'T CHANGE THE LOCATIONS OF THE INPUTS AND OUTPUTS!
  //   OUTPUT from your circuit
endmodule
