// Logisim project regfile.circ as structural Verilog: 1 circuit, main circuit main
module main (
  input  [4:0] rs1,
  input  [4:0] rs2,
  input  [4:0] rd,
  input  [31:0] Write_Data,
  input  RegWEn,
  input  clk,
  output [31:0] ra,
  output [31:0] sp,
  output [31:0] t0,
  output [31:0] t1,
  output [31:0] t2,
  output [31:0] s0,
  output [31:0] s1,
  output [31:0] a0,
  output [31:0] Read_Data_1,
  output [31:0] Read_Data_2
);

  wire a0_t, ra_t, s0_t, s1_t, sp_t, t0_t, t1_t, t2_t;
  wire [4:0] and_1_out, multiplexer_1_out;
  wire [31:0] and_2_out, and_3_out, and_4_out, and_5_out, and_6_out, and_7_out, and_8_out, and_9_out,
       and_10_out, and_11_out, and_12_out, and_13_out, and_14_out, and_15_out, and_16_out, and_17_out,
       multiplexer_4_out, multiplexer_5_out, multiplexer_6_out, multiplexer_7_out, multiplexer_8_out,
       multiplexer_9_out, multiplexer_10_out, multiplexer_11_out, nor_2_out, nor_4_out, nor_6_out, nor_8_out,
       nor_10_out, nor_12_out, nor_14_out, nor_16_out, not_1_out, not_2_out, not_3_out, not_4_out, not_5_out,
       not_6_out, not_7_out, not_8_out;

  Multiplexer #(.width(5), .enable("false")) multiplexer_1 (
    .in0({5{1'b0}}), .in1({5{1'b1}}), .out(multiplexer_1_out), .sel(RegWEn));
  Multiplexer #(.select(5), .width(32), .enable("false")) multiplexer_2 (
    .in0({32{1'b0}}), .in1(ra), .in2(sp), .in3(t0), .in4(t1), .in5(t2), .in6(s0), .in7(s1), .in8(a0),
    .out(Read_Data_1), .sel(rs1));  // open: in9, in10, in11, in12, in13, in14, in15, in16, in17, in18, in19, in20, in21, in22, in23, in24, in25, in26, in27, in28, in29, in30, in31
  Demultiplexer #(.select(5)) demultiplexer_1 (
    .out1(ra_t), .out2(sp_t), .out3(t0_t), .out4(t1_t), .out5(t2_t), .out6(s0_t), .out7(s1_t), .out8(a0_t),
    .in(1'b1), .sel(and_1_out), .en(clk));  // open: out0, out9, out10, out11, out12, out13, out14, out15, out16, out17, out18, out19, out20, out21, out22, out23, out24, out25, out26, out27, out28, out29, out30, out31
  assign and_1_out = multiplexer_1_out & rd;  // AND_Gate and_1, 5 bits wide
  Multiplexer #(.select(5), .width(32), .enable("false")) multiplexer_3 (
    .in0({32{1'b0}}), .in1(ra), .in2(sp), .in3(t0), .in4(t1), .in5(t2), .in6(s0), .in7(s1), .in8(a0),
    .out(Read_Data_2), .sel(rs2));  // open: in9, in10, in11, in12, in13, in14, in15, in16, in17, in18, in19, in20, in21, in22, in23, in24, in25, in26, in27, in28, in29, in30, in31
  Multiplexer #(.width(32), .enable("false")) multiplexer_4 (
    .in0({32{1'b0}}), .in1({32{1'b1}}), .out(multiplexer_4_out), .sel(ra_t));
  Multiplexer #(.width(32), .enable("false")) multiplexer_5 (
    .in0({32{1'b0}}), .in1({32{1'b1}}), .out(multiplexer_5_out), .sel(sp_t));
  Multiplexer #(.width(32), .enable("false")) multiplexer_6 (
    .in0({32{1'b0}}), .in1({32{1'b1}}), .out(multiplexer_6_out), .sel(t0_t));
  Multiplexer #(.width(32), .enable("false")) multiplexer_7 (
    .in0({32{1'b0}}), .in1({32{1'b1}}), .out(multiplexer_7_out), .sel(t1_t));
  assign not_1_out = ~Write_Data;  // NOT_Gate not_1, 32 bits wide
  assign not_2_out = ~Write_Data;  // NOT_Gate not_2, 32 bits wide
  assign not_3_out = ~Write_Data;  // NOT_Gate not_3, 32 bits wide
  assign not_4_out = ~Write_Data;  // NOT_Gate not_4, 32 bits wide
  assign and_2_out = multiplexer_4_out & not_1_out;  // AND_Gate and_2, 32 bits wide
  assign and_3_out = multiplexer_4_out & Write_Data;  // AND_Gate and_3, 32 bits wide
  assign and_4_out = multiplexer_5_out & not_2_out;  // AND_Gate and_4, 32 bits wide
  assign and_5_out = multiplexer_5_out & Write_Data;  // AND_Gate and_5, 32 bits wide
  assign and_6_out = multiplexer_6_out & not_3_out;  // AND_Gate and_6, 32 bits wide
  assign and_7_out = multiplexer_6_out & Write_Data;  // AND_Gate and_7, 32 bits wide
  assign and_8_out = multiplexer_7_out & not_4_out;  // AND_Gate and_8, 32 bits wide
  assign and_9_out = multiplexer_7_out & Write_Data;  // AND_Gate and_9, 32 bits wide
  assign ra = ~(and_2_out | nor_2_out);  // NOR_Gate nor_1, 32 bits wide
  assign nor_2_out = ~(ra | and_3_out);  // NOR_Gate nor_2, 32 bits wide
  assign sp = ~(and_4_out | nor_4_out);  // NOR_Gate nor_3, 32 bits wide
  assign nor_4_out = ~(sp | and_5_out);  // NOR_Gate nor_4, 32 bits wide
  assign t0 = ~(and_6_out | nor_6_out);  // NOR_Gate nor_5, 32 bits wide
  assign nor_6_out = ~(t0 | and_7_out);  // NOR_Gate nor_6, 32 bits wide
  assign t1 = ~(and_8_out | nor_8_out);  // NOR_Gate nor_7, 32 bits wide
  assign nor_8_out = ~(t1 | and_9_out);  // NOR_Gate nor_8, 32 bits wide
  Multiplexer #(.width(32), .enable("false")) multiplexer_8 (
    .in0({32{1'b0}}), .in1({32{1'b1}}), .out(multiplexer_8_out), .sel(t2_t));
  Multiplexer #(.width(32), .enable("false")) multiplexer_9 (
    .in0({32{1'b0}}), .in1({32{1'b1}}), .out(multiplexer_9_out), .sel(s0_t));
  Multiplexer #(.width(32), .enable("false")) multiplexer_10 (
    .in0({32{1'b0}}), .in1({32{1'b1}}), .out(multiplexer_10_out), .sel(s1_t));
  Multiplexer #(.width(32), .enable("false")) multiplexer_11 (
    .in0({32{1'b0}}), .in1({32{1'b1}}), .out(multiplexer_11_out), .sel(a0_t));
  assign not_5_out = ~Write_Data;  // NOT_Gate not_5, 32 bits wide
  assign not_6_out = ~Write_Data;  // NOT_Gate not_6, 32 bits wide
  assign not_7_out = ~Write_Data;  // NOT_Gate not_7, 32 bits wide
  assign not_8_out = ~Write_Data;  // NOT_Gate not_8, 32 bits wide
  assign and_10_out = multiplexer_8_out & not_5_out;  // AND_Gate and_10, 32 bits wide
  assign and_11_out = multiplexer_8_out & Write_Data;  // AND_Gate and_11, 32 bits wide
  assign and_12_out = multiplexer_9_out & not_6_out;  // AND_Gate and_12, 32 bits wide
  assign and_13_out = multiplexer_9_out & Write_Data;  // AND_Gate and_13, 32 bits wide
  assign and_14_out = multiplexer_10_out & not_7_out;  // AND_Gate and_14, 32 bits wide
  assign and_15_out = multiplexer_10_out & Write_Data;  // AND_Gate and_15, 32 bits wide
  assign and_16_out = multiplexer_11_out & not_8_out;  // AND_Gate and_16, 32 bits wide
  assign and_17_out = multiplexer_11_out & Write_Data;  // AND_Gate and_17, 32 bits wide
  assign t2 = ~(and_10_out | nor_10_out);  // NOR_Gate nor_9, 32 bits wide
  assign nor_10_out = ~(t2 | and_11_out);  // NOR_Gate nor_10, 32 bits wide
  assign s0 = ~(and_12_out | nor_12_out);  // NOR_Gate nor_11, 32 bits wide
  assign nor_12_out = ~(s0 | and_13_out);  // NOR_Gate nor_12, 32 bits wide
  assign s1 = ~(and_14_out | nor_14_out);  // NOR_Gate nor_13, 32 bits wide
  assign nor_14_out = ~(s1 | and_15_out);  // NOR_Gate nor_14, 32 bits wide
  assign a0 = ~(and_16_out | nor_16_out);  // NOR_Gate nor_15, 32 bits wide
  assign nor_16_out = ~(a0 | and_17_out);  // NOR_Gate nor_16, 32 bits wide

  // Other names for the same wires on the sheet: read_data1[31:0] = Read_Data_1; read_data2[31:0] = Read_Data_2;
  //   read_reg1[4:0] = rs1; read_reg2[4:0] = rs2; write_en = RegWEn; write_reg[4:0] = rd

  // Notes on the sheet:
  //   INPUTS to your circuit
  //   DON'T CHANGE THE LOCATIONS OF THE INPUTS AND OUTPUTS!
  //   These are DEBUG/TEST outputs from your circuit.
  //   OUTPUTS from your circuit
endmodule
